# Fritzing sketch breadboard_view-01 (saved by Fritzing 0.9.3b)
breadboards: 2

parts:
  U1 = NodeMCU V3.0
  FET1 = STP16NF06 N-Channel Power MOSFET
  FET2 = STP16NF06 N-Channel Power MOSFET
  FET3 = STP16NF06 N-Channel Power MOSFET
  FET4 = STP16NF06 N-Channel Power MOSFET

nets:
  N1: U1.D0, FET4.gate
  N2: U1.D1, FET3.gate
  N3: U1.D2, FET2.gate
  N4: U1.D3, FET1.gate
  N5: U1.3V3, FET1.source, FET2.source, FET3.source, FET4.source
  N6: U1.GND#6, U1.GND#13, U1.GND#16, U1.GND#33

notes:
  Common ground
  To lights
  +12V to lights

custom parts:
  NodeMCU V3.0: ESP8266 based NodeMCU
  STP16NF06 N-Channel Power MOSFET: STP16NF06 N-channel Power MOSFET
