# Fritzing sketch breadboard_view-03 (saved by Fritzing 0.9.3b)
breadboards: 3

parts:
  U1 = NodeMCU V3.0
  FET1 = STP16NF06 N-Channel Power MOSFET
  FET2 = STP16NF06 N-Channel Power MOSFET
  FET3 = STP16NF06 N-Channel Power MOSFET
  FET4 = STP16NF06 N-Channel Power MOSFET
  FET5 = STP16NF06 N-Channel Power MOSFET
  FET6 = STP16NF06 N-Channel Power MOSFET
  FET7 = STP16NF06 N-Channel Power MOSFET
  FET8 = STP16NF06 N-Channel Power MOSFET
  U2 = Voltage Regulator - 5V [package="TO220 [THT]"]
  C1 = Electrolytic Capacitor [capacitance=10µF package="100 mil [THT, electrolytic]"]
  C2 = Electrolytic Capacitor [capacitance=1µF package="100 mil [THT, electrolytic]"]

nets:
  N1: U1.D0, FET4.gate
  N2: U1.D1, FET3.gate
  N3: U1.D2, FET2.gate
  N4: U1.D3, FET1.gate
  N5: U1.D4, FET8.gate
  N6: U1.GND#6, U1.GND#13, U1.GND#16, U1.GND#33, FET1.source, FET2.source, FET3.source, FET4.source, FET5.source, FET6.source, FET7.source, FET8.source, U2.GND, C1.-, C2.-
  N7: U1.D5, FET7.gate
  N8: U1.D6, FET6.gate
  N9: U1.D7, FET5.gate
  N10: U1.Vin, U2.output_voltage, C2.+
  N11: U2.input_voltage, C1.+

notes:
  Common ground
  To lights
  +12V in
  +12V to lights

custom parts:
  NodeMCU V3.0: ESP8266 based NodeMCU
  STP16NF06 N-Channel Power MOSFET: STP16NF06 N-channel Power MOSFET
