# Fritzing sketch 01-MCU_board (saved by Fritzing 0.9.3b)
circuit board: 8.46667cm x 5.64444cm

parts:
  U1 = NodeMCU V3.0
  J1 = Camdenboss CTB0158-2 [part_number=CTB0158-2 package=THT]
  J2 = male pin header, 5 pins [form="♂ (male)"]
  J3 = male pin header, 5 pins [form="♂ (male)"]
  U2 = Voltage Regulator - 5V [package="TO220 [THT]"]
  C4 = Electrolytic Capacitor [capacitance=10µF package="100 mil [THT, electrolytic]"]
  C5 = Electrolytic Capacitor [capacitance=1µF package="100 mil [THT, electrolytic]"]

nets:
  N1: U1.D0, J2.pin1
  N2: U1.D1, J2.pin2
  N3: U1.D2, J2.pin3
  N4: U1.D3, J2.pin4
  N5: U1.D4, J3.pin1
  GND: U1.GND, J1.pin1, J2.pin5, J3.pin5, U2.GND, C4.+, C5.-
  N6: U1.D5, J3.pin2
  N7: U1.D6, J3.pin3
  N8: U1.D7, J3.pin4
  N9: U1.Vin, U2.output_voltage, C5.+
  N10: J1.pin2, U2.input_voltage, C4.-

custom parts:
  NodeMCU V3.0: ESP8266 based NodeMCU
