# Fritzing sketch 02-FET_board (saved by Fritzing 0.9.3b)
circuit board: 5.64444cm x 8.46667cm

parts:
  FET2 = STP16NF06 N-Channel Power MOSFET
  FET4 = STP16NF06 N-Channel Power MOSFET
  FET7 = STP16NF06 N-Channel Power MOSFET
  FET8 = STP16NF06 N-Channel Power MOSFET
  FET1 = STP16NF06 N-Channel Power MOSFET
  FET6 = STP16NF06 N-Channel Power MOSFET
  FET5 = STP16NF06 N-Channel Power MOSFET
  FET3 = STP16NF06 N-Channel Power MOSFET
  LED_power = Camdenboss CTB0158-2 [part_number=CTB0158-2 package=THT]
  Output_3 = male pin header, 2 pins [form="♂ (male)"]
  Output_4 = male pin header, 2 pins [form="♂ (male)"]
  Output_2 = male pin header, 2 pins [form="♂ (male)"]
  Output_1 = male pin header, 2 pins [form="♂ (male)"]
  J1 = male pin header, 5 pins [form="♂ (male)"]
  J2 = male pin header, 5 pins [form="♂ (male)"]

nets:
  N1: FET2.gate, J1.pin2
  N2: FET2.drain, Output_1.pin1
  N3: FET2.source, FET4.source, FET7.source, FET8.source, FET1.source, FET6.source, FET5.source, FET3.source, LED_power.pin2, J1.pin3, J2.pin3
  N4: FET4.gate, J1.pin4
  N5: FET4.drain, Output_2.pin1
  N6: FET7.gate, J2.pin5
  N7: FET7.drain, Output_4.pin2
  N8: FET8.gate, J2.pin4
  N9: FET8.drain, Output_4.pin1
  N10: FET1.gate, J1.pin1
  N11: FET1.drain, Output_1.pin2
  N12: FET6.gate, J2.pin2
  N13: FET6.drain, Output_3.pin1
  N14: FET5.gate, J2.pin1
  N15: FET5.drain, Output_3.pin2
  N16: FET3.gate, J1.pin5
  N17: FET3.drain, Output_2.pin2

custom parts:
  STP16NF06 N-Channel Power MOSFET: STP16NF06 N-channel Power MOSFET
